// Logisim project IT012_Lab01_25520249.circ as structural Verilog
module Warmup (
  input  A,
  input  B,
  output out_3
);

  wire not_1_out;

  not not_1 (not_1_out, B);
  and and_1 (out_3, A, not_1_out);
endmodule

module TN1 (
  input  A,
  input  B,
  input  C,
  output out_4,
  output out_5,
  output out_6,
  output out_7,
  output out_8,
  output out_9,
  output out_10,
  output out_11,
  output out_12,
  output Y
);

  wire X_out;

  not not_1 (out_4, A);
  and and_1 (out_5, A, B);
  or or_1 (out_6, A, B);
  nand nand_1 (out_7, A, B);
  nor nor_1 (out_8, A, B);
  xor xor_1 (out_9, A, B);
  xnor xnor_1 (out_10, A, B);
  ExactlyOne XOR3 (.out(out_11), .in0(A), .in1(B), .in2(C));
  nand NAND3 (out_12, A, B, C);
  nand X (X_out, A, B);
  nand nand_2 (Y, X_out, C);
endmodule

module TN2 (
  input  X,
  input  Y,
  input  Z,
  output EQ1,
  output EQ2,
  output EQ3,
  output EQ4,
  output EQ5
);

  wire and_1_out, and_2_out, and_3_out, and_4_out, and_5_out, nand_1_out, nor_1_out, not_1_out, not_2_out,
       not_3_out, or_1_out, or_2_out, or_3_out, or_4_out, or_5_out;

  not not_1 (not_1_out, X);
  and and_1 (and_1_out, not_1_out, Y);
  nand nand_1 (nand_1_out, X, Y);
  and and_2 (and_2_out, Y, Z);
  or or_1 (or_1_out, X, Y);
  or or_2 (or_2_out, X, Z);
  not not_2 (not_2_out, X);
  not not_3 (not_3_out, Y);
  or or_3 (or_3_out, X, and_1_out);
  or or_4 (or_4_out, X, Z);
  and and_3 (and_3_out, not_2_out, not_3_out);
  or or_5 (or_5_out, and_2_out, X);
  and and_4 (and_4_out, or_1_out, or_2_out);
  nor nor_1 (nor_1_out, X, Y);
  and and_5 (and_5_out, not_2_out, not_3_out);
  xnor xnor_1 (EQ1, nor_1_out, and_5_out);
  xnor xnor_2 (EQ2, nand_1_out, and_3_out);
  xnor xnor_3 (EQ3, or_5_out, and_4_out);
  xnor xnor_4 (EQ4, X, or_3_out);
  xnor xnor_5 (EQ5, or_3_out, or_4_out);
endmodule

module TN3 (
  input  A,
  input  B,
  input  C,
  input  D,
  output F
);

  wire and_1_out, and_2_out, and_3_out, and_4_out, and_5_out, and_6_out, not_1_out, not_2_out, not_3_out,
       not_4_out;

  not not_1 (not_1_out, A);
  and and_1 (and_1_out, not_1_out, not_2_out, C, not_4_out);
  not not_2 (not_2_out, B);
  and and_2 (and_2_out, not_1_out, not_2_out, C, D);
  not not_3 (not_3_out, C);
  and and_3 (and_3_out, not_1_out, B, not_3_out, D);
  not not_4 (not_4_out, D);
  and and_4 (and_4_out, not_1_out, B, C, D);
  or or_1 (F, and_1_out, and_2_out, and_3_out, and_4_out, and_5_out, and_6_out);
  and and_5 (and_5_out, A, not_2_out, C, D);
  and and_6 (and_6_out, A, B, not_3_out, D);
endmodule

module TN4 (
  input  A,
  input  B,
  input  C,
  input  D,
  output F_SoP,
  output F_PoS,
  output F_can,
  output EQ1,
  output EQ2
);

  wire and_1_out, and_2_out, and_3_out, and_4_out, and_5_out, and_6_out, and_7_out, and_8_out, and_9_out,
       and_10_out, not_1_out, not_2_out, not_3_out, not_4_out, or_3_out, or_4_out, or_5_out, or_6_out,
       or_7_out;

  not not_1 (not_1_out, A);
  not not_2 (not_2_out, B);
  and and_1 (and_1_out, not_1_out, not_2_out, C, not_4_out);
  not not_3 (not_3_out, C);
  and and_2 (and_2_out, not_1_out, not_2_out, C, D);
  not not_4 (not_4_out, D);
  and and_3 (and_3_out, not_1_out, B, not_3_out, D);
  or or_1 (F_can, and_1_out, and_2_out, and_3_out, and_4_out, and_5_out, and_6_out);
  and and_4 (and_4_out, not_1_out, B, C, D);
  and and_5 (and_5_out, A, not_2_out, C, D);
  and and_6 (and_6_out, A, B, not_3_out, D);
  xnor xnor_1 (EQ1, F_can, F_SoP);
  and and_7 (and_7_out, not_1_out, not_2_out, C);
  and and_8 (and_8_out, not_1_out, B, D);
  or or_2 (F_SoP, and_7_out, and_8_out, and_9_out, and_10_out);
  and and_9 (and_9_out, B, not_3_out, D);
  and and_10 (and_10_out, not_2_out, C, D);
  xnor xnor_2 (EQ2, F_can, F_PoS);
  or or_3 (or_3_out, B, C);
  or or_4 (or_4_out, C, D);
  or or_5 (or_5_out, not_1_out, D);
  or or_6 (or_6_out, not_2_out, D);
  and and_11 (F_PoS, or_3_out, or_4_out, or_6_out, or_5_out, or_7_out);
  or or_7 (or_7_out, not_1_out, not_2_out, not_3_out);
endmodule

module TN5 (
  input  C,
  input  B,
  input  A,
  output F
);

  wire xor_1_out;

  xor xor_1 (xor_1_out, B, A);
  xor xor_2 (F, C, xor_1_out);
endmodule
